# Fritzing sketch ESP32_i2c_multi (saved by Fritzing 0.9.3b)
circuit board: 8.2cm x 6cm
breadboards: 1

parts:
  TCA9548A = Adafruit TCA9548A
  J2 = shrouded pin header, 16 pins [form="♂ (shrouded male)"]
  J1 = shrouded pin header, 16 pins [form="♂ (shrouded male)"]
  ESP32 = DOIT Esp32 DevKit v1 (30 pins long, 11 pins width) [part_number=ESP32S-PIN30]

nets:
  N1: TCA9548A.2SDA, J1.pin14
  N2: TCA9548A.2SCL, J1.pin3
  N3: TCA9548A.3SDA, J1.pin16
  N4: TCA9548A.3SCL, J1.pin1
  N5: TCA9548A.4SDA, J2.pin16
  N6: TCA9548A.4SCL, J2.pin1
  N7: TCA9548A.5SDA, J2.pin14
  N8: TCA9548A.5SCL, J2.pin3
  N9: TCA9548A.6SDA, J2.pin12
  N10: TCA9548A.6SCL, J2.pin5
  N11: TCA9548A.7SDA, J2.pin10
  N12: TCA9548A.7SCL, J2.pin7
  VCC: TCA9548A.VCC, J2.pin2, J2.pin4, J2.pin6, J2.pin8, J1.pin2, J1.pin4, J1.pin6, J1.pin8, ESP32.3V3
  GND: TCA9548A.GND, J2.pin9, J2.pin11, J2.pin13, J2.pin15, J1.pin9, J1.pin11, J1.pin13, J1.pin15, ESP32.GND
  N13: TCA9548A.INPUTSDA, ESP32.D21
  N14: TCA9548A.INPUTSCL, ESP32.D22
  N15: TCA9548A.0SDA, J1.pin10
  N16: TCA9548A.0SCL, J1.pin7
  N17: TCA9548A.1SDA, J1.pin12
  N18: TCA9548A.1SCL, J1.pin5

notes:
  Multi-sensor
  monitoring module V1.0
  mohammad.kareem@cern.ch

custom parts:
  Adafruit TCA9548A: You just found the perfect I2C sensor, and you want to wire up two or three or more of them to your Arduino when you realize "Uh oh, this chip has a fixed I2C address, and from what I know about I2C, you cannot have two devices with the same address on the same SDA/SCL pins!" Are you out of luck? You would be, if you didn't have this ultra-cool TCA9548A 1-to-8 I2C multiplexer! Finally, a way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
  DOIT Esp32 DevKit v1 (30 pins long, 11 pins width): The DOIT Esp32 DevKit v1 is one of the development board created by DOIT to evaluate the ESP-WROOM-32 module. It is based on the ESP32 microcontroller that boasts Wifi, Bluetooth, Ethernet and Low Power support all in a single chip. (vanepp) made breadboard work, adjusted pin numbering and labels and reduced size of schematic and cleaned up pcb. This chip is 30pins long (2 x15) and 11 pins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
