# Fritzing sketch esp32_single (saved by Fritzing 0.9.3b)
circuit board: 3.26775cm x 7.74941cm
breadboards: 1

parts:
  ESP32 = DOIT Esp32 DevKit v1 (30 pins long, 11 pins width) [part_number=ESP32S-PIN30]
  SHT = Compass Module - HMC6352

nets:
  3V3: ESP32.3V3, SHT.VCC
  GND: ESP32.GND, SHT.GND
  N1: ESP32.D21, SHT.SDA
  N2: ESP32.D22, SHT.SCL

notes:
  VIN
  GND
  VCC
  SDA
  SCL
  Single-sensor
  monitoring module V1.1
  mohammad.kareem@cern.ch

custom parts:
  DOIT Esp32 DevKit v1 (30 pins long, 11 pins width): The DOIT Esp32 DevKit v1 is one of the development board created by DOIT to evaluate the ESP-WROOM-32 module. It is based on the ESP32 microcontroller that boasts Wifi, Bluetooth, Ethernet and Low Power support all in a single chip. (vanepp) made breadboard work, adjusted pin numbering and labels and reduced size of schematic and cleaned up pcb. This chip is 30pins long (2 x15) and 11 pins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
